# Fritzing sketch RGBserial-with-bluetooth (saved by Fritzing 0.9.3b)
breadboards: 1

parts:
  Q1 = NPN-Transistor [package="TO92 [THT]"]
  Q2 = NPN-Transistor [package="TO92 [THT]"]
  Q3 = NPN-Transistor [package="TO92 [THT]"]
  Part1 = Arduino Uno (Rev3)
  Part2 = Bluetooth HC-05 Macho
  Power_plug1 = Power plug
  S1 = SPST Switch [package=switch-spst-smd-a]

nets:
  N1: Q1.B, Part1.D3_PWM
  GND: Q1.C, Q2.C, Q3.C, Part1.GND, Part2.GND, Power_plug1.GND, S1.S
  N2: Q2.B, Part1.D5_PWM
  N3: Q3.B, Part1.D6_PWM
  N4: Part1.D0/RX, S1.O
  N5: Part1.D1/TX, Part2.RXD
  3V3: Part1.3V3, Part2.VCC
  N6: Part2.TXD, S1.P

notes:
  These are the red, green and blue wires that go to the LED strip
  And this is the positive 9-12V that goes to the strip
  This is the power input source (9V or 12V)
