# Fritzing sketch RGBserial-without-bluetooth (saved by Fritzing 0.9.3b)
breadboards: 1

parts:
  Q1 = NPN-Transistor [package="TO92 [THT]"]
  Q2 = NPN-Transistor [package="TO92 [THT]"]
  Q3 = NPN-Transistor [package="TO92 [THT]"]
  Part1 = Arduino Uno (Rev3)
  Power_plug1 = Power plug

nets:
  N1: Q1.B, Part1.D3_PWM
  GND: Q1.C, Q2.C, Q3.C, Part1.GND, Power_plug1.GND
  N2: Q2.B, Part1.D5_PWM
  N3: Q3.B, Part1.D6_PWM

notes:
  These are the red, green and blue wires that go to the LED strip
  And this is the positive 9-12V that goes to the strip
  This is the power input source (9V or 12V)
